// Logisim project Real_alu.circ as structural Verilog
module And (
  input  [3:0] A,
  input  [3:0] B,
  output [3:0] out_3
);

  assign out_3 = A & B;  // AND_Gate and_1, 4 bits wide
endmodule
